// Logisim project RISC_processor_for_simulation.circ as structural Verilog: 20 circuits, main circuit Top_level_processor_with_wrapper
module CPU_main (
  input  CPU_EN,
  input  ASYN_CLR,
  output [7:0] PC_OUT,
  output [3:0] FLAG_OUT,
  output DOUT,
  output [7:0] OUT_RESULT
);

  wire CLK_out, PROCESSOR_CTRL_UNIT_1_pc_reg_en, PROCESSOR_CTRL_UNIT_1_pc_src_sel,
       PROCESSOR_CTRL_UNIT_1_reg_in_bus_src_sel, PROCESSOR_CTRL_UNIT_1_rom_clken, RAM_INTERFACE_1_ram_wren,
       REG_INPUT_BUS_ENABLE_out;
  wire [1:0] PROCESSOR_CTRL_UNIT_1_b_bus_src_sel;
  wire [3:0] ALU_1_flag, PROCESSOR_CTRL_UNIT_1_op0_reg_out_sel, PROCESSOR_CTRL_UNIT_1_op1_reg_out_sel,
       PROCESSOR_CTRL_UNIT_1_ram_int_ctrl, PROCESSOR_CTRL_UNIT_1_reg_rd_sel;
  wire [8:0] PROCESSOR_CTRL_UNIT_1_alu_ctrl;
  wire [9:0] RAM_INTERFACE_1_addr_out;
  wire [9:8] CPU_REGISTERS_1_pc_bus;
  wire [12:0] ROM_QUARTUS_16_1_data_out;
  wire [21:0] CPU_REGISTERS_1_pc_bus_2;
  wire [31:0] adder_1_out, ALU_1_result, CPU_REGISTERS_1_op0_out_bus, CPU_REGISTERS_1_op1_out_bus,
       multiplexer_1_out, multiplexer_2_out, multiplexer_3_out, RAM_QUARTUS_16_1_data_out;
  wire [31:13] ROM_QUARTUS_16_1_data_out_2;

  Clock CLK (.out(CLK_out));
  Multiplexer #(.width(32), .enable("false")) multiplexer_1 (
    .in0(adder_1_out), .in1(ALU_1_result), .out(multiplexer_1_out), .sel(PROCESSOR_CTRL_UNIT_1_pc_src_sel));
  nand REG_INPUT_BUS_ENABLE (REG_INPUT_BUS_ENABLE_out, PROCESSOR_CTRL_UNIT_1_reg_rd_sel[0], PROCESSOR_CTRL_UNIT_1_reg_rd_sel[1], PROCESSOR_CTRL_UNIT_1_reg_rd_sel[2], PROCESSOR_CTRL_UNIT_1_reg_rd_sel[3]);
  Adder #(.width(32)) adder_1 (
    .a({CPU_REGISTERS_1_pc_bus_2, CPU_REGISTERS_1_pc_bus, PC_OUT}), .b(32'h1), .out(adder_1_out), .cin(1'b0));  // open: cout
  ROM_QUARTUS_16 ROM_QUARTUS_16_1 (
    .ADDR_IN({CPU_REGISTERS_1_pc_bus, PC_OUT}), .CLKEN(PROCESSOR_CTRL_UNIT_1_rom_clken), .CLK(CLK_out),
    .DATA_OUT({ROM_QUARTUS_16_1_data_out_2, ROM_QUARTUS_16_1_data_out}));
  CPU_REGISTERS CPU_REGISTERS_1 (
    .REG_INPUT_BUS(multiplexer_3_out), .REG_ACLR(ASYN_CLR), .REG_WR_SEL(PROCESSOR_CTRL_UNIT_1_reg_rd_sel),
    .PC_ACLR(ASYN_CLR), .PC_IN_BUS(multiplexer_1_out), .PC_REG_EN(PROCESSOR_CTRL_UNIT_1_pc_reg_en),
    .OP1_REG_OUT_SEL(PROCESSOR_CTRL_UNIT_1_op1_reg_out_sel),
    .OP0_REG_OUT_SEL(PROCESSOR_CTRL_UNIT_1_op0_reg_out_sel), .CLK(CLK_out),
    .OP1_OUT_BUS(CPU_REGISTERS_1_op1_out_bus), .OP0_OUT_BUS(CPU_REGISTERS_1_op0_out_bus),
    .PC_BUS({CPU_REGISTERS_1_pc_bus_2, CPU_REGISTERS_1_pc_bus, PC_OUT}));
  PROCESSOR_CTRL_UNIT PROCESSOR_CTRL_UNIT_1 (
    .CLK(CLK_out), .ASYS_CLR(ASYN_CLR), .CPU_EN(CPU_EN),
    .INSTRUCTION({ROM_QUARTUS_16_1_data_out_2, ROM_QUARTUS_16_1_data_out}), .RESULT_FLAG(ALU_1_flag),
    .ROM_CLKEN(PROCESSOR_CTRL_UNIT_1_rom_clken), .RAM_INT_CTRL(PROCESSOR_CTRL_UNIT_1_ram_int_ctrl),
    .PC_SRC_SEL(PROCESSOR_CTRL_UNIT_1_pc_src_sel), .PC_REG_EN(PROCESSOR_CTRL_UNIT_1_pc_reg_en),
    .REG_RD_SEL(PROCESSOR_CTRL_UNIT_1_reg_rd_sel), .OP0_REG_OUT_SEL(PROCESSOR_CTRL_UNIT_1_op0_reg_out_sel),
    .OP1_REG_OUT_SEL(PROCESSOR_CTRL_UNIT_1_op1_reg_out_sel),
    .B_BUS_SRC_SEL(PROCESSOR_CTRL_UNIT_1_b_bus_src_sel),
    .REG_IN_BUS_SRC_SEL(PROCESSOR_CTRL_UNIT_1_reg_in_bus_src_sel), .DOUT(DOUT),
    .ALU_CTRL(PROCESSOR_CTRL_UNIT_1_alu_ctrl), .FLAG_OUT(FLAG_OUT));
  Multiplexer #(.select(2), .width(32), .enable("false")) multiplexer_2 (
    .in0(CPU_REGISTERS_1_op1_out_bus), .in1({{19{1'b0}}, ROM_QUARTUS_16_1_data_out}), .in2({32{1'b1}}),
    .out(multiplexer_2_out), .sel(PROCESSOR_CTRL_UNIT_1_b_bus_src_sel));  // open: in3
  ALU ALU_1 (
    .RESULT(ALU_1_result), .FLAG(ALU_1_flag), .OP1_B_BUS(multiplexer_2_out),
    .ALU_CTRL_BUS(PROCESSOR_CTRL_UNIT_1_alu_ctrl), .OP0_A_BUS(CPU_REGISTERS_1_op0_out_bus));
  Multiplexer #(.width(32)) multiplexer_3 (
    .in0(ALU_1_result), .in1(RAM_QUARTUS_16_1_data_out), .out(multiplexer_3_out),
    .sel(PROCESSOR_CTRL_UNIT_1_reg_in_bus_src_sel), .en(REG_INPUT_BUS_ENABLE_out));
  Multiplexer #(.width(8)) multiplexer_4 (
    .in1(ALU_1_result[7:0]), .out(OUT_RESULT), .sel(DOUT), .en(DOUT));  // open: in0
  RAM_INTERFACE RAM_INTERFACE_1 (
    .ADDR_IN(ALU_1_result[9:0]), .CLK(CLK_out), .RAM_INT_CTRL(PROCESSOR_CTRL_UNIT_1_ram_int_ctrl),
    .ADDR_OUT(RAM_INTERFACE_1_addr_out), .RAM_WREN(RAM_INTERFACE_1_ram_wren));
  RAM_QUARTUS_16 RAM_QUARTUS_16_1 (
    .ADDR_IN(RAM_INTERFACE_1_addr_out), .RAM_WREN(RAM_INTERFACE_1_ram_wren), .CLK(CLK_out),
    .DATA_IN(ALU_1_result), .ACLR(ASYN_CLR), .DATA_OUT(RAM_QUARTUS_16_1_data_out));
endmodule

module RAM_CPU (
  input  [9:0] wraddress,
  input  [9:0] rdaddress,
  input  wren,
  input  clock,
  input  [31:0] data,
  input  aclr,
  output [31:0] q
);

  RAM #(.addrWidth(10), .dataWidth(32), .databus("bibus")) ram_1 (
    .addr(wraddress), .we(wren), .oe(1'b1), .clk(clock), .din(data), .dout(q));
endmodule

module ROM_CPU (
  input  [9:0] address,
  input  clken,
  input  clock,
  output [31:0] q
);

  wire [9:0] register_1_q;

  Register #(.width(10)) register_1 (.D(address), .en(clken), .clk(clock), .Q(register_1_q), .clr(1'b0));
  ROM #(.addrWidth(10), .dataWidth(32)) rom_1 (.addr(register_1_q), .data(q));

  // Notes on the sheet:
  //   contents of rom_1 (hex, n*v repeats v):
  //   eb400004 eb402001 e1004200 e0a06400 ab5e801f e0c24000 eb400006 ec822001 eb5ea015 e61fea00 eb5e6000
  //   e35ede00 e0800400 e9066001 eaa1e000 e1000200 c61fec00 e68be600 e6de0a00 e61fea00 e75ffe00 e71fe000
  //   e65ffe00
endmodule

module Top_level_processor_with_wrapper (
  input  Input_1,
  input  Input_2,
  output Output_1,
  output Output_2,
  output Output_3
);

  CPU_main CPU_main_1 (.CPU_EN(Input_1), .ASYN_CLR(Input_2), .DOUT(Output_1));  // open: PC_OUT, FLAG_OUT, OUT_RESULT

  assign Output_2 = Output_1;
  assign Output_3 = Output_1;
endmodule

module State_machine_provided (
  input  CLK,
  input  STATE_CLR,
  input  CPU_EN,
  input  COND_MATCH,
  input  [31:0] INST,
  output [3:0] STATE,
  output ROM_EN,
  output PC_REG_EN,
  output PC_SRC_SEL,
  output [3:0] RAM_INT_CTRL
);

  wire [3:0] undriven;

  Register #(.width(4)) register_1 (.D(undriven), .en(1'b1), .clk(CLK), .Q(STATE), .clr(STATE_CLR));
endmodule

module RAM_QUARTUS_16 (
  input  [9:0] ADDR_IN,
  input  RAM_WREN,
  input  CLK,
  input  [31:0] DATA_IN,
  input  ACLR,
  output [31:0] DATA_OUT
);

  RAM_CPU RAM_CPU_1 (
    .aclr(ACLR), .data(DATA_IN), .clock(CLK), .wren(RAM_WREN), .rdaddress(ADDR_IN), .wraddress(ADDR_IN),
    .q(DATA_OUT));
endmodule

module CTRL_CIRCUIT_PROVIDED (
  input  [3:0] STATE,
  input  [31:0] INST,
  input  C_FLAG,
  output [8:0] ALU_CTRL,
  output [2:0] FLAG_REG_CTRL,
  output [3:0] RD_OUT,
  output [3:0] OP0_REG_OUT_SEL,
  output [3:0] OP1_REG_OUT_SEL,
  output [1:0] B_BUS_SRC_SEL,
  output REG_INPUT_SRC_SEL,
  output DOUT
);

  wire and_1_out, and_2_out, and_3_out, and_4_out, and_5_out, and_6_out, and_7_out, and_8_out, and_9_out,
       and_10_out, and_11_out, and_12_out, and_13_out, and_14_out, and_15_out, and_16_out, and_17_out,
       and_18_out, and_19_out, and_20_out, and_21_out, and_22_out, and_25_out, and_26_out, and_27_out,
       and_28_out, and_29_out, and_30_out, and_31_out, and_32_out, and_33_out, and_34_out, and_35_out,
       and_36_out, and_37_out, and_38_out, and_39_out, and_40_out, and_42_out, and_43_out, and_44_out,
       and_45_out, and_49_out, and_50_out, nand_1_out, nand_2_out, not_1_out, not_2_out, not_3_out,
       not_4_out, not_5_out, not_6_out, not_7_out, not_8_out, not_9_out, not_10_out, not_11_out, not_12_out,
       not_13_out, not_14_out, not_15_out, not_16_out, not_17_out, not_18_out, not_19_out, not_20_out,
       not_21_out, not_22_out, not_23_out, not_24_out, not_25_out, not_26_out, not_27_out, not_28_out,
       not_29_out, not_30_out, not_31_out, not_32_out, not_33_out, not_34_out, not_35_out, not_36_out,
       not_37_out, not_38_out, not_39_out, not_40_out, not_41_out, not_42_out, not_43_out, not_44_out,
       not_45_out, not_46_out, not_47_out, not_48_out, not_49_out, not_50_out, not_51_out, not_52_out,
       not_53_out, not_54_out, not_55_out, not_56_out, not_57_out, not_58_out, not_59_out, not_60_out,
       not_61_out, not_62_out, not_63_out, not_64_out, not_65_out, not_66_out, not_67_out, not_68_out,
       not_69_out, not_70_out, not_71_out, not_72_out, not_73_out, not_74_out, not_75_out, not_76_out,
       not_77_out, not_78_out, not_79_out, not_80_out, not_81_out, not_82_out, not_83_out, not_84_out,
       not_85_out, not_86_out, not_87_out, not_88_out, not_89_out, not_90_out, not_91_out, not_92_out,
       not_93_out, not_94_out, not_95_out, not_96_out, not_97_out, not_98_out, not_99_out, not_100_out,
       not_101_out, not_102_out, not_103_out, not_104_out, not_105_out, not_106_out, not_107_out,
       not_108_out, not_109_out, not_110_out, not_111_out, not_112_out, not_113_out, not_114_out,
       not_115_out, not_116_out, not_117_out, not_118_out, not_119_out, not_120_out, not_121_out,
       not_122_out, not_123_out, not_124_out, not_125_out, not_126_out, not_127_out, not_128_out,
       not_129_out, not_130_out, not_131_out, not_132_out, not_133_out, not_134_out, not_135_out,
       not_136_out, not_137_out, not_138_out, not_139_out, not_140_out, not_141_out, not_142_out,
       not_143_out, not_144_out, not_145_out, not_146_out, not_147_out, not_148_out, not_149_out,
       not_150_out, not_151_out, not_152_out, not_153_out, not_154_out, not_155_out, not_156_out,
       not_157_out, not_158_out, not_159_out, not_160_out, not_161_out, not_162_out, not_163_out,
       not_164_out, not_165_out, not_166_out, not_167_out, not_168_out, not_169_out, not_170_out,
       not_171_out, not_172_out, not_173_out, not_174_out, not_175_out, not_176_out, not_177_out,
       not_178_out, not_179_out, not_180_out, not_181_out, not_182_out, not_183_out, not_184_out,
       not_185_out, not_186_out, not_187_out, not_188_out, not_189_out, or_1_out;
  wire [1:0] and_41_out, or_13_out;

  not not_1 (not_1_out, INST[23]);
  not not_2 (not_2_out, INST[26]);
  not not_3 (not_3_out, INST[24]);
  not not_4 (not_4_out, INST[23]);
  not not_5 (not_5_out, INST[23]);
  not not_6 (not_6_out, STATE[3]);
  not not_7 (not_7_out, STATE[2]);
  not not_8 (not_8_out, STATE[1]);
  not not_9 (not_9_out, STATE[2]);
  not not_10 (not_10_out, STATE[1]);
  not not_11 (not_11_out, INST[26]);
  not not_12 (not_12_out, INST[24]);
  not not_13 (not_13_out, INST[23]);
  not not_14 (not_14_out, STATE[2]);
  not not_15 (not_15_out, STATE[1]);
  not not_16 (not_16_out, STATE[2]);
  not not_17 (not_17_out, STATE[1]);
  not not_18 (not_18_out, INST[24]);
  not not_19 (not_19_out, INST[22]);
  not not_20 (not_20_out, STATE[2]);
  not not_21 (not_21_out, STATE[1]);
  not not_22 (not_22_out, INST[23]);
  not not_23 (not_23_out, INST[22]);
  not not_24 (not_24_out, STATE[2]);
  not not_25 (not_25_out, STATE[1]);
  not not_26 (not_26_out, STATE[2]);
  not not_27 (not_27_out, STATE[1]);
  not not_28 (not_28_out, STATE[2]);
  not not_29 (not_29_out, STATE[1]);
  not not_30 (not_30_out, STATE[0]);
  not not_31 (not_31_out, INST[25]);
  not not_32 (not_32_out, INST[24]);
  not not_33 (not_33_out, STATE[2]);
  not not_34 (not_34_out, STATE[1]);
  not not_35 (not_35_out, STATE[0]);
  not not_36 (not_36_out, INST[25]);
  not not_37 (not_37_out, INST[22]);
  not not_38 (not_38_out, STATE[2]);
  not not_39 (not_39_out, STATE[1]);
  not not_40 (not_40_out, STATE[0]);
  not not_41 (not_41_out, INST[25]);
  not not_42 (not_42_out, INST[23]);
  not not_43 (not_43_out, STATE[2]);
  not not_44 (not_44_out, STATE[1]);
  not not_45 (not_45_out, STATE[0]);
  not not_46 (not_46_out, INST[25]);
  not not_47 (not_47_out, INST[22]);
  not not_48 (not_48_out, STATE[2]);
  not not_49 (not_49_out, STATE[1]);
  not not_50 (not_50_out, STATE[0]);
  not not_51 (not_51_out, INST[25]);
  not not_52 (not_52_out, INST[22]);
  not not_53 (not_53_out, STATE[2]);
  not not_54 (not_54_out, STATE[1]);
  not not_55 (not_55_out, STATE[0]);
  not not_56 (not_56_out, INST[26]);
  not not_57 (not_57_out, INST[25]);
  not not_58 (not_58_out, INST[23]);
  not not_59 (not_59_out, C_FLAG);
  not not_60 (not_60_out, STATE[2]);
  not not_61 (not_61_out, STATE[1]);
  not not_62 (not_62_out, STATE[0]);
  not not_63 (not_63_out, INST[26]);
  not not_64 (not_64_out, INST[25]);
  not not_65 (not_65_out, STATE[2]);
  not not_66 (not_66_out, STATE[1]);
  not not_67 (not_67_out, STATE[0]);
  not not_68 (not_68_out, INST[26]);
  not not_69 (not_69_out, INST[25]);
  not not_70 (not_70_out, INST[25]);
  not not_71 (not_71_out, INST[24]);
  not not_72 (not_72_out, STATE[2]);
  not not_73 (not_73_out, STATE[1]);
  not not_74 (not_74_out, STATE[0]);
  not not_75 (not_75_out, INST[26]);
  not not_76 (not_76_out, INST[22]);
  not not_77 (not_77_out, STATE[2]);
  not not_78 (not_78_out, STATE[1]);
  not not_79 (not_79_out, STATE[0]);
  not not_80 (not_80_out, INST[26]);
  not not_81 (not_81_out, INST[24]);
  not not_82 (not_82_out, STATE[2]);
  not not_83 (not_83_out, STATE[1]);
  not not_84 (not_84_out, STATE[0]);
  not not_85 (not_85_out, INST[26]);
  not not_86 (not_86_out, STATE[2]);
  not not_87 (not_87_out, STATE[1]);
  not not_88 (not_88_out, STATE[0]);
  not not_89 (not_89_out, INST[26]);
  not not_90 (not_90_out, INST[24]);
  not not_91 (not_91_out, STATE[2]);
  not not_92 (not_92_out, STATE[1]);
  not not_93 (not_93_out, STATE[0]);
  not not_94 (not_94_out, INST[26]);
  not not_95 (not_95_out, INST[25]);
  not not_96 (not_96_out, STATE[2]);
  not not_97 (not_97_out, STATE[1]);
  not not_98 (not_98_out, STATE[0]);
  not not_99 (not_99_out, INST[26]);
  not not_100 (not_100_out, INST[25]);
  not not_101 (not_101_out, INST[24]);
  not not_102 (not_102_out, STATE[2]);
  not not_103 (not_103_out, STATE[1]);
  not not_104 (not_104_out, STATE[0]);
  not not_105 (not_105_out, INST[25]);
  not not_106 (not_106_out, INST[22]);
  not not_107 (not_107_out, STATE[2]);
  not not_108 (not_108_out, STATE[1]);
  not not_109 (not_109_out, STATE[0]);
  not not_110 (not_110_out, INST[26]);
  not not_111 (not_111_out, INST[24]);
  not not_112 (not_112_out, STATE[2]);
  not not_113 (not_113_out, STATE[1]);
  not not_114 (not_114_out, STATE[0]);
  not not_115 (not_115_out, INST[26]);
  not not_116 (not_116_out, INST[25]);
  not not_117 (not_117_out, STATE[2]);
  not not_118 (not_118_out, STATE[1]);
  not not_119 (not_119_out, STATE[0]);
  not not_120 (not_120_out, INST[26]);
  not not_121 (not_121_out, INST[25]);
  not not_122 (not_122_out, INST[24]);
  not not_123 (not_123_out, STATE[3]);
  not not_124 (not_124_out, STATE[2]);
  not not_125 (not_125_out, STATE[0]);
  not not_126 (not_126_out, STATE[3]);
  not not_127 (not_127_out, STATE[2]);
  not not_128 (not_128_out, STATE[1]);
  not not_129 (not_129_out, STATE[0]);
  not not_130 (not_130_out, INST[26]);
  not not_131 (not_131_out, INST[25]);
  not not_132 (not_132_out, STATE[2]);
  not not_133 (not_133_out, STATE[1]);
  not not_134 (not_134_out, STATE[0]);
  not not_135 (not_135_out, INST[26]);
  not not_136 (not_136_out, STATE[2]);
  not not_137 (not_137_out, STATE[1]);
  not not_138 (not_138_out, STATE[0]);
  not not_139 (not_139_out, INST[25]);
  not not_140 (not_140_out, INST[24]);
  not not_141 (not_141_out, STATE[2]);
  not not_142 (not_142_out, STATE[1]);
  not not_143 (not_143_out, STATE[0]);
  not not_144 (not_144_out, INST[25]);
  not not_145 (not_145_out, INST[23]);
  not not_146 (not_146_out, STATE[2]);
  not not_147 (not_147_out, STATE[1]);
  not not_148 (not_148_out, STATE[0]);
  not not_149 (not_149_out, INST[25]);
  not not_150 (not_150_out, INST[22]);
  not not_151 (not_151_out, STATE[3]);
  not not_152 (not_152_out, STATE[2]);
  not not_153 (not_153_out, STATE[0]);
  not not_154 (not_154_out, STATE[3]);
  not not_155 (not_155_out, STATE[2]);
  not not_156 (not_156_out, INST[24]);
  not not_157 (not_157_out, INST[23]);
  not not_158 (not_158_out, STATE[3]);
  not not_159 (not_159_out, STATE[2]);
  not not_160 (not_160_out, STATE[0]);
  not not_161 (not_161_out, STATE[3]);
  not not_162 (not_162_out, STATE[1]);
  not not_163 (not_163_out, STATE[0]);
  not not_164 (not_164_out, STATE[3]);
  not not_165 (not_165_out, STATE[2]);
  not not_166 (not_166_out, STATE[0]);
  not not_167 (not_167_out, STATE[2]);
  not not_168 (not_168_out, STATE[1]);
  not not_169 (not_169_out, STATE[0]);
  not not_170 (not_170_out, INST[26]);
  not not_171 (not_171_out, INST[26]);
  not not_172 (not_172_out, STATE[3]);
  not not_173 (not_173_out, STATE[1]);
  not not_174 (not_174_out, STATE[0]);
  not not_175 (not_175_out, STATE[3]);
  and and_1 (and_1_out, INST[25], INST[24], not_1_out, INST[22]);
  not not_176 (not_176_out, STATE[3]);
  and and_2 (and_2_out, not_2_out, not_3_out, not_4_out, INST[22]);
  and and_3 (and_3_out, INST[25], INST[24], not_5_out);
  and and_4 (and_4_out, INST[25], INST[24], INST[22]);
  and and_5 (and_5_out, INST[26], INST[24], INST[23], INST[22]);
  and and_6 (and_6_out, INST[26], INST[25]);
  and and_7 (and_7_out, not_6_out, not_7_out, not_8_out);
  and and_8 (and_8_out, not_9_out, not_10_out, not_11_out, not_12_out, not_13_out);
  and and_9 (and_9_out, not_14_out, not_15_out, INST[25], INST[24], INST[23]);
  and and_10 (and_10_out, not_16_out, not_17_out, INST[26], not_18_out, not_19_out);
  and and_11 (and_11_out, not_20_out, not_21_out, INST[26], not_22_out, not_23_out);
  and and_12 (and_12_out, not_24_out, not_25_out, INST[26], INST[24], INST[23], INST[22]);
  and and_13 (and_13_out, not_26_out, not_27_out, INST[26], INST[25]);
  and and_14 (and_14_out, STATE[3], STATE[0]);
  and and_15 (and_15_out, STATE[3], STATE[1]);
  and and_16 (and_16_out, STATE[3], not_28_out, not_29_out, not_30_out, INST[26], not_31_out, not_32_out, INST[23]);
  and and_17 (and_17_out, STATE[3], not_33_out, not_34_out, not_35_out, INST[26], not_36_out, INST[23], not_37_out);
  and and_18 (and_18_out, STATE[3], not_38_out, not_39_out, not_40_out, INST[26], not_41_out, INST[24], not_42_out);
  and and_19 (and_19_out, STATE[3], not_43_out, not_44_out, not_45_out, INST[26], not_46_out, INST[24], not_47_out);
  and and_20 (and_20_out, C_FLAG, STATE[3], not_48_out, not_49_out, not_50_out, INST[26], not_51_out, INST[24], INST[23], not_52_out);
  and and_21 (and_21_out, C_FLAG, STATE[3], not_53_out, not_54_out, not_55_out, not_56_out, not_57_out, INST[24], not_58_out, INST[22]);
  and and_22 (and_22_out, not_59_out, STATE[3], not_60_out, not_61_out, not_62_out, not_63_out, not_64_out, INST[24], INST[23]);
  and and_23 (ALU_CTRL[6], STATE[3], not_65_out, not_66_out, not_67_out, not_68_out, not_69_out, INST[23], INST[22]);
  not not_177 (not_177_out, INST[22]);
  or or_1 (or_1_out, not_70_out, not_71_out);
  not not_178 (not_178_out, INST[26]);
  not not_179 (not_179_out, STATE[0]);
  not not_180 (not_180_out, STATE[1]);
  not not_181 (not_181_out, STATE[2]);
  and and_24 (ALU_CTRL[8], STATE[3], not_72_out, not_73_out, not_74_out, not_75_out, INST[25], INST[24], INST[23], not_76_out);
  and and_25 (and_25_out, STATE[3], not_77_out, not_78_out, not_79_out, not_80_out, INST[25], not_81_out);
  and and_26 (and_26_out, INST[21], STATE[3], not_82_out, not_83_out, not_84_out, not_85_out);
  and and_27 (and_27_out, STATE[3], not_86_out, not_87_out, not_88_out, not_89_out, INST[25], not_90_out, INST[23]);
  and and_28 (and_28_out, INST[21], STATE[3], not_91_out, not_92_out, not_93_out, not_94_out, not_95_out, INST[24]);
  and and_29 (and_29_out, INST[21], STATE[3], not_96_out, not_97_out, not_98_out, not_99_out, not_100_out, not_101_out, INST[23]);
  and and_30 (and_30_out, STATE[3], not_102_out, not_103_out, not_104_out, INST[26], not_105_out, INST[24], INST[23], not_106_out);
  and and_31 (and_31_out, STATE[3], not_107_out, not_108_out, not_109_out, not_110_out, INST[25], not_111_out, INST[23]);
  and and_32 (and_32_out, INST[21], STATE[3], not_112_out, not_113_out, not_114_out, not_115_out, not_116_out, INST[24]);
  and and_33 (and_33_out, INST[21], STATE[3], not_117_out, not_118_out, not_119_out, not_120_out, not_121_out, not_122_out, INST[23]);
  and and_34 (and_34_out, not_123_out, not_124_out, STATE[1], not_125_out);
  and and_35 (and_35_out, not_126_out, STATE[2], STATE[1], STATE[0]);
  and and_36 (and_36_out, STATE[3], not_127_out, not_128_out, not_129_out, not_130_out, not_131_out);
  and and_37 (and_37_out, STATE[3], not_132_out, not_133_out, not_134_out, not_135_out, INST[25], INST[24]);
  and and_38 (and_38_out, STATE[3], not_136_out, not_137_out, not_138_out, INST[26], not_139_out, not_140_out);
  and and_39 (and_39_out, STATE[3], not_141_out, not_142_out, not_143_out, INST[26], not_144_out, INST[24], not_145_out);
  and and_40 (and_40_out, STATE[3], not_146_out, not_147_out, not_148_out, INST[26], not_149_out, INST[24], INST[23], not_150_out);
  and and_41 (and_41_out[0], not_151_out, not_152_out, STATE[1], not_153_out);
  and and_42 (and_42_out, not_154_out, not_155_out, STATE[1], STATE[0], INST[26], INST[25], not_156_out, not_157_out, INST[22]);
  and and_43 (and_43_out, not_158_out, not_159_out, STATE[1], not_160_out);
  and and_44 (and_44_out, not_161_out, STATE[2], not_162_out, not_163_out);
  and and_45 (and_45_out, not_164_out, not_165_out, STATE[1], not_166_out);
  and and_46 (B_BUS_SRC_SEL[1], STATE[3], not_167_out, not_168_out, not_169_out, not_170_out, INST[25], INST[24], INST[23], INST[22]);
  not not_182 (not_182_out, STATE[2]);
  not not_183 (not_183_out, STATE[1]);
  not not_184 (not_184_out, STATE[0]);
  not not_185 (not_185_out, INST[26]);
  nand nand_1 (nand_1_out, not_171_out, INST[25], INST[24], INST[23], INST[22]);
  not not_186 (not_186_out, STATE[2]);
  not not_187 (not_187_out, STATE[1]);
  not not_188 (not_188_out, STATE[0]);
  not not_189 (not_189_out, INST[25]);
  nand nand_2 (nand_2_out, INST[24], INST[23], INST[22]);
  and and_47 (REG_INPUT_SRC_SEL, not_172_out, STATE[2], STATE[1], STATE[0]);
  or or_2 (ALU_CTRL[2], not_175_out, and_1_out, INST[26], STATE[0], STATE[1], STATE[2]);
  or or_3 (ALU_CTRL[1], not_176_out, and_2_out, and_3_out, and_4_out, and_5_out, and_6_out, STATE[0], STATE[1], STATE[2]);
  or or_4 (ALU_CTRL[0], and_7_out, and_8_out, and_9_out, and_10_out, and_11_out, and_12_out, and_13_out, and_14_out, and_15_out);
  or or_5 (ALU_CTRL[4], and_16_out, and_17_out);
  or or_6 (ALU_CTRL[3], and_18_out, and_19_out);
  or or_7 (ALU_CTRL[5], and_20_out, and_21_out, and_22_out);
  and and_48 (ALU_CTRL[7], STATE[3], INST[23], not_177_out, or_1_out, not_178_out, not_179_out, not_180_out, not_181_out);
  or or_8 (FLAG_REG_CTRL[0], and_25_out, and_26_out);
  or or_9 (FLAG_REG_CTRL[1], and_27_out, and_28_out, and_29_out, and_30_out);
  or or_10 (FLAG_REG_CTRL[2], and_31_out, and_32_out, and_33_out);
  or or_11 (and_41_out[1], and_34_out, and_35_out, and_36_out, and_37_out, and_38_out, and_39_out, and_40_out);
  or or_12 (or_13_out[1], and_42_out, and_43_out);
  or or_13 (or_13_out[0], and_44_out, and_45_out);
  and and_49 (and_49_out, INST[27], STATE[3], not_182_out, not_183_out, not_184_out, not_185_out, nand_1_out);
  and and_50 (and_50_out, INST[27], STATE[3], not_186_out, not_187_out, not_188_out, INST[26], not_189_out, nand_2_out);
  and and_51 (DOUT, STATE[3], STATE[2], not_173_out, not_174_out);
  or or_14 (B_BUS_SRC_SEL[0], and_49_out, and_50_out);
  Multiplexer #(.select(2), .width(4), .enable("false")) multiplexer_1 (
    .in0(4'b1111), .in1(4'b1111), .in2(INST[16:13]), .in3(4'b1110), .out(RD_OUT), .sel(and_41_out));
  Multiplexer #(.select(2), .width(4), .enable("false")) multiplexer_2 (
    .in0(INST[12:9]), .in1(INST[20:17]), .in2(4'b1110), .in3(4'b1111), .out(OP1_REG_OUT_SEL), .sel(or_13_out));

  assign OP0_REG_OUT_SEL = INST[20:17];
endmodule

module RAM_INTERFACE (
  input  [9:0] ADDR_IN,
  input  CLK,
  input  [3:0] RAM_INT_CTRL,
  output [9:0] ADDR_OUT,
  output RAM_WREN
);

  wire [9:0] register_1_q;

  Register #(.width(10)) register_1 (.D(ADDR_IN), .en(RAM_INT_CTRL[1]), .clk(CLK), .Q(register_1_q), .clr(1'b0));
  Multiplexer #(.width(10)) multiplexer_1 (
    .in0(ADDR_IN), .in1(register_1_q), .out(ADDR_OUT), .sel(RAM_INT_CTRL[2]), .en(RAM_INT_CTRL[3]));

  assign RAM_WREN = RAM_INT_CTRL[0];
endmodule

module ROM_QUARTUS_16 (
  input  [9:0] ADDR_IN,
  input  CLKEN,
  input  CLK,
  output [31:0] DATA_OUT
);

  ROM_CPU ROM_CPU_1 (.q(DATA_OUT), .clock(CLK), .clken(CLKEN), .address(ADDR_IN));
endmodule

module FLAG_REGISTER (
  input  [2:0] FLAG_EN_CTRL,
  input  [3:0] FLAG_IN,
  input  CLR_FLAG,
  input  CLK,
  output [3:0] FLAG_OUT
);

  Register #(.width(1)) register_1 (.D(FLAG_IN[3]), .en(FLAG_EN_CTRL[0]), .clk(CLK), .Q(FLAG_OUT[3]), .clr(CLR_FLAG));
  Register #(.width(1)) register_2 (.D(FLAG_IN[2]), .en(FLAG_EN_CTRL[0]), .clk(CLK), .Q(FLAG_OUT[2]), .clr(CLR_FLAG));
  Register #(.width(1)) register_3 (.D(FLAG_IN[1]), .en(FLAG_EN_CTRL[1]), .clk(CLK), .Q(FLAG_OUT[1]), .clr(CLR_FLAG));
  Register #(.width(1)) register_4 (.D(FLAG_IN[0]), .en(FLAG_EN_CTRL[2]), .clk(CLK), .Q(FLAG_OUT[0]), .clr(CLR_FLAG));
endmodule

module RIGHT_SHIFT_BLOCK (
  input  [31:0] OP_IN,
  input  [4:0] SHIFT_DISTANCE,
  input  [1:0] SHIFT_FUNC_SEL,
  input  CIN,
  output [31:0] RESULT,
  output COUT
);

  wire [31:0] shifter_1_out, shifter_2_out, shifter_3_out;

  Shifter #(.width(32), .shift("lr")) shifter_1 (.in(OP_IN), .\dist (SHIFT_DISTANCE), .out(shifter_1_out));
  Shifter #(.width(32), .shift("ar")) shifter_2 (.in(OP_IN), .\dist (SHIFT_DISTANCE), .out(shifter_2_out));
  Shifter #(.width(32), .shift("rr")) shifter_3 (.in(OP_IN), .\dist (SHIFT_DISTANCE), .out(shifter_3_out));
  Multiplexer #(.select(2), .width(32), .enable("false")) multiplexer_1 (
    .in0(shifter_1_out), .in1(shifter_2_out), .in2(shifter_3_out), .in3({CIN, OP_IN[31:1]}), .out(RESULT),
    .sel(SHIFT_FUNC_SEL));

  assign COUT = OP_IN[0];
endmodule

module LEFT_SHIFT_BLOCK (
  input  [31:0] OP_IN,
  input  [4:0] SHIFT_DISTANCE,
  input  [1:0] SHIFT_FUNC_SEL,
  output [31:0] RESULT
);

  wire [31:0] shifter_1_out, shifter_2_out;

  Shifter #(.width(32)) shifter_1 (.in(OP_IN), .\dist (SHIFT_DISTANCE), .out(shifter_1_out));
  Shifter #(.width(32), .shift("rl")) shifter_2 (.in(OP_IN), .\dist (SHIFT_DISTANCE), .out(shifter_2_out));
  Multiplexer #(.width(32), .enable("false")) multiplexer_1 (
    .in0(shifter_1_out), .in1(shifter_2_out), .out(RESULT), .sel(SHIFT_FUNC_SEL[1]));
endmodule

module CPU_REGISTERS (
  input  [31:0] REG_INPUT_BUS,
  input  REG_ACLR,
  input  [3:0] REG_WR_SEL,
  input  PC_ACLR,
  input  [31:0] PC_IN_BUS,
  input  PC_REG_EN,
  input  [3:0] OP1_REG_OUT_SEL,
  input  [3:0] OP0_REG_OUT_SEL,
  input  CLK,
  output [31:0] OP1_OUT_BUS,
  output [31:0] OP0_OUT_BUS,
  output [31:0] PC_BUS
);

  wire decoder_1_out0, decoder_1_out1, decoder_1_out2, decoder_1_out3, decoder_1_out4, decoder_1_out5,
       decoder_1_out6, decoder_1_out7, decoder_1_out8, decoder_1_out9, decoder_1_out10, decoder_1_out11,
       decoder_1_out12, decoder_1_out13, decoder_1_out14;
  wire [31:0] R0_q, R1_q, R2_q, R3_q, R4_q, R5_q, R6_q, R7_q, R8_q, R9_q, R10_q, R11_q, R12_q, R13_q, R14_q;

  Decoder #(.select(4), .enable("false")) decoder_1 (
    .out0(decoder_1_out0), .out1(decoder_1_out1), .out2(decoder_1_out2), .out3(decoder_1_out3),
    .out4(decoder_1_out4), .out5(decoder_1_out5), .out6(decoder_1_out6), .out7(decoder_1_out7),
    .out8(decoder_1_out8), .out9(decoder_1_out9), .out10(decoder_1_out10), .out11(decoder_1_out11),
    .out12(decoder_1_out12), .out13(decoder_1_out13), .out14(decoder_1_out14), .sel(REG_WR_SEL));  // open: out15
  Register #(.width(32)) R0 (.D(REG_INPUT_BUS), .en(decoder_1_out0), .clk(CLK), .Q(R0_q), .clr(REG_ACLR));
  Register #(.width(32)) R1 (.D(REG_INPUT_BUS), .en(decoder_1_out1), .clk(CLK), .Q(R1_q), .clr(REG_ACLR));
  Register #(.width(32)) R2 (.D(REG_INPUT_BUS), .en(decoder_1_out2), .clk(CLK), .Q(R2_q), .clr(REG_ACLR));
  Register #(.width(32)) R3 (.D(REG_INPUT_BUS), .en(decoder_1_out3), .clk(CLK), .Q(R3_q), .clr(REG_ACLR));
  Register #(.width(32)) R4 (.D(REG_INPUT_BUS), .en(decoder_1_out4), .clk(CLK), .Q(R4_q), .clr(REG_ACLR));
  Register #(.width(32)) R5 (.D(REG_INPUT_BUS), .en(decoder_1_out5), .clk(CLK), .Q(R5_q), .clr(REG_ACLR));
  Register #(.width(32)) R6 (.D(REG_INPUT_BUS), .en(decoder_1_out6), .clk(CLK), .Q(R6_q), .clr(REG_ACLR));
  Register #(.width(32)) R7 (.D(REG_INPUT_BUS), .en(decoder_1_out7), .clk(CLK), .Q(R7_q), .clr(REG_ACLR));
  Register #(.width(32)) R8 (.D(REG_INPUT_BUS), .en(decoder_1_out8), .clk(CLK), .Q(R8_q), .clr(REG_ACLR));
  Register #(.width(32)) R9 (.D(REG_INPUT_BUS), .en(decoder_1_out9), .clk(CLK), .Q(R9_q), .clr(REG_ACLR));
  Register #(.width(32)) R10 (.D(REG_INPUT_BUS), .en(decoder_1_out10), .clk(CLK), .Q(R10_q), .clr(CLK));
  Register #(.width(32)) R11 (.D(REG_INPUT_BUS), .en(decoder_1_out11), .clk(CLK), .Q(R11_q), .clr(REG_ACLR));
  Register #(.width(32)) R12 (.D(REG_INPUT_BUS), .en(decoder_1_out12), .clk(CLK), .Q(R12_q), .clr(REG_ACLR));
  Register #(.width(32)) R13 (.D(REG_INPUT_BUS), .en(decoder_1_out13), .clk(CLK), .Q(R13_q), .clr(REG_ACLR));
  Register #(.width(32)) R14 (.D(REG_INPUT_BUS), .en(decoder_1_out14), .clk(CLK), .Q(R14_q), .clr(REG_ACLR));
  Register #(.width(32)) PC_REG (.D(PC_IN_BUS), .en(PC_REG_EN), .clk(CLK), .Q(PC_BUS), .clr(PC_ACLR));
  Multiplexer #(.select(4), .width(32), .enable("false")) multiplexer_1 (
    .in0(R0_q), .in1(R1_q), .in2(R2_q), .in3(R3_q), .in4(R4_q), .in5(R5_q), .in6(R6_q), .in7(R7_q),
    .in8(R8_q), .in9(R9_q), .in10(R10_q), .in11(R11_q), .in12(R12_q), .in13(R13_q), .in14(R14_q),
    .in15(PC_BUS), .out(OP1_OUT_BUS), .sel(OP1_REG_OUT_SEL));
  Multiplexer #(.select(4), .width(32), .enable("false")) multiplexer_2 (
    .in0(R0_q), .in1(R1_q), .in2(R2_q), .in3(R3_q), .in4(R4_q), .in5(R5_q), .in6(R6_q), .in7(R7_q),
    .in8(R8_q), .in9(R9_q), .in10(R10_q), .in11(R11_q), .in12(R12_q), .in13(R13_q), .in14(R14_q),
    .in15(PC_BUS), .out(OP0_OUT_BUS), .sel(OP0_REG_OUT_SEL));
endmodule

module COND_FLAG_CHK (
  input  [3:0] CONDITION_IN,
  input  [3:0] FLAG_IN,
  output CONDITION_MATCHED
);

  wire and_1_out, and_2_out, and_3_out, and_4_out, and_5_out, and_6_out, and_7_out, and_8_out, and_9_out,
       and_10_out, and_11_out, and_12_out, and_13_out, and_14_out, and_15_out, and_16_out, and_17_out,
       and_18_out, not_1_out, not_2_out, not_3_out, not_4_out, not_5_out, not_6_out, not_7_out, not_8_out,
       not_9_out, not_10_out, not_11_out, not_12_out, not_13_out, not_14_out, not_15_out, not_16_out,
       not_17_out, not_18_out, not_19_out, not_20_out, not_21_out, not_22_out, not_23_out, not_24_out,
       not_25_out, not_26_out, not_27_out, not_28_out, not_29_out, not_30_out, not_31_out, not_32_out,
       not_33_out, not_34_out, not_35_out, not_36_out, not_37_out, not_38_out, not_39_out, not_40_out,
       not_41_out, not_42_out, not_43_out, not_44_out, not_45_out, not_46_out, not_47_out;

  not not_1 (not_1_out, CONDITION_IN[3]);
  not not_2 (not_2_out, CONDITION_IN[2]);
  not not_3 (not_3_out, CONDITION_IN[1]);
  not not_4 (not_4_out, CONDITION_IN[0]);
  not not_5 (not_5_out, CONDITION_IN[3]);
  not not_6 (not_6_out, CONDITION_IN[2]);
  not not_7 (not_7_out, CONDITION_IN[1]);
  not not_8 (not_8_out, FLAG_IN[2]);
  not not_9 (not_9_out, CONDITION_IN[2]);
  not not_10 (not_10_out, CONDITION_IN[1]);
  not not_11 (not_11_out, FLAG_IN[2]);
  not not_12 (not_12_out, FLAG_IN[1]);
  not not_13 (not_13_out, CONDITION_IN[3]);
  not not_14 (not_14_out, CONDITION_IN[2]);
  not not_15 (not_15_out, CONDITION_IN[0]);
  not not_16 (not_16_out, CONDITION_IN[3]);
  not not_17 (not_17_out, CONDITION_IN[2]);
  not not_18 (not_18_out, FLAG_IN[1]);
  not not_19 (not_19_out, CONDITION_IN[3]);
  not not_20 (not_20_out, CONDITION_IN[1]);
  not not_21 (not_21_out, CONDITION_IN[0]);
  not not_22 (not_22_out, CONDITION_IN[0]);
  not not_23 (not_23_out, FLAG_IN[2]);
  not not_24 (not_24_out, CONDITION_IN[3]);
  not not_25 (not_25_out, CONDITION_IN[1]);
  not not_26 (not_26_out, FLAG_IN[3]);
  not not_27 (not_27_out, CONDITION_IN[0]);
  not not_28 (not_28_out, CONDITION_IN[3]);
  not not_29 (not_29_out, FLAG_IN[0]);
  not not_30 (not_30_out, CONDITION_IN[2]);
  not not_31 (not_31_out, CONDITION_IN[1]);
  not not_32 (not_32_out, CONDITION_IN[0]);
  not not_33 (not_33_out, FLAG_IN[2]);
  not not_34 (not_34_out, CONDITION_IN[1]);
  not not_35 (not_35_out, CONDITION_IN[0]);
  not not_36 (not_36_out, FLAG_IN[3]);
  not not_37 (not_37_out, FLAG_IN[0]);
  not not_38 (not_38_out, CONDITION_IN[0]);
  not not_39 (not_39_out, CONDITION_IN[2]);
  not not_40 (not_40_out, FLAG_IN[0]);
  not not_41 (not_41_out, CONDITION_IN[0]);
  not not_42 (not_42_out, FLAG_IN[3]);
  not not_43 (not_43_out, FLAG_IN[2]);
  not not_44 (not_44_out, FLAG_IN[0]);
  not not_45 (not_45_out, CONDITION_IN[1]);
  not not_46 (not_46_out, FLAG_IN[0]);
  not not_47 (not_47_out, CONDITION_IN[0]);
  and and_1 (and_1_out, not_1_out, not_2_out, not_3_out, not_4_out, FLAG_IN[2]);
  and and_2 (and_2_out, not_5_out, not_6_out, not_7_out, CONDITION_IN[0], not_8_out);
  and and_3 (and_3_out, not_9_out, not_10_out, CONDITION_IN[0], not_11_out, not_12_out);
  and and_4 (and_4_out, not_13_out, not_14_out, CONDITION_IN[1], not_15_out, FLAG_IN[1]);
  and and_5 (and_5_out, not_16_out, not_17_out, CONDITION_IN[1], CONDITION_IN[0], not_18_out);
  and and_6 (and_6_out, not_19_out, CONDITION_IN[2], not_20_out, not_21_out, FLAG_IN[3]);
  and and_7 (and_7_out, CONDITION_IN[2], not_22_out, FLAG_IN[3], not_23_out, FLAG_IN[0]);
  and and_8 (and_8_out, not_24_out, CONDITION_IN[2], not_25_out, CONDITION_IN[0], not_26_out);
  and and_9 (and_9_out, CONDITION_IN[2], CONDITION_IN[1], not_27_out, FLAG_IN[0]);
  and and_10 (and_10_out, not_28_out, CONDITION_IN[2], CONDITION_IN[1], CONDITION_IN[0], not_29_out);
  and and_11 (and_11_out, CONDITION_IN[3], not_30_out, not_31_out, not_32_out, not_33_out, FLAG_IN[1]);
  and and_12 (and_12_out, CONDITION_IN[3], not_34_out, CONDITION_IN[0], FLAG_IN[2]);
  and and_13 (and_13_out, CONDITION_IN[3], CONDITION_IN[1], not_35_out, not_36_out, not_37_out);
  and and_14 (and_14_out, CONDITION_IN[3], CONDITION_IN[1], not_38_out, FLAG_IN[3], FLAG_IN[0]);
  and and_15 (and_15_out, CONDITION_IN[3], not_39_out, CONDITION_IN[1], CONDITION_IN[0], FLAG_IN[3], not_40_out);
  and and_16 (and_16_out, CONDITION_IN[3], CONDITION_IN[2], not_41_out, not_42_out, not_43_out, not_44_out);
  and and_17 (and_17_out, CONDITION_IN[3], CONDITION_IN[2], not_45_out, CONDITION_IN[0], FLAG_IN[3], not_46_out);
  and and_18 (and_18_out, CONDITION_IN[3], CONDITION_IN[2], CONDITION_IN[1], not_47_out);
  or or_1 (CONDITION_MATCHED, and_1_out, and_2_out, and_3_out, and_4_out, and_5_out, and_6_out, and_7_out, and_8_out, and_9_out, and_10_out, and_11_out, and_12_out, and_13_out, and_14_out, and_15_out, and_16_out, and_17_out, and_18_out);
endmodule

module ALU (
  input  [8:0] ALU_CTRL_BUS,
  input  [31:0] OP1_B_BUS,
  input  [31:0] OP0_A_BUS,
  output [3:0] FLAG,
  output [31:0] RESULT
);

  wire ALU_ADDER_1_cout, and_2_out, RIGHT_SHIFT_BLOCK_1_cout;
  wire [31:0] ALU_ADDER_1_result, and_1_out, LEFT_SHIFT_BLOCK_1_result, multiplexer_1_out, not_1_out,
       or_1_out, RIGHT_SHIFT_BLOCK_1_result, xor_1_out;

  Multiplexer #(.width(32), .enable("false")) multiplexer_1 (
    .in0(OP1_B_BUS), .in1(not_1_out), .out(multiplexer_1_out), .sel(ALU_CTRL_BUS[8]));
  assign not_1_out = ~OP1_B_BUS;  // NOT_Gate not_1, 32 bits wide
  assign and_1_out = OP0_A_BUS & multiplexer_1_out;  // AND_Gate and_1, 32 bits wide
  assign or_1_out = OP0_A_BUS | OP1_B_BUS;  // OR_Gate or_1, 32 bits wide
  assign xor_1_out = OP0_A_BUS ^ OP1_B_BUS;  // XOR_Gate xor_1, 32 bits wide
  ALU_ADDER ALU_ADDER_1 (
    .Cin(ALU_CTRL_BUS[5]), .RSB(ALU_CTRL_BUS[6]), .SUB(ALU_CTRL_BUS[7]), .OP0(OP0_A_BUS), .OP1(OP1_B_BUS),
    .RESULT(ALU_ADDER_1_result), .Cout(ALU_ADDER_1_cout), .V(FLAG[0]));
  RIGHT_SHIFT_BLOCK RIGHT_SHIFT_BLOCK_1 (
    .OP_IN(OP0_A_BUS), .SHIFT_DISTANCE(OP1_B_BUS[4:0]), .SHIFT_FUNC_SEL(ALU_CTRL_BUS[4:3]),
    .CIN(ALU_CTRL_BUS[5]), .RESULT(RIGHT_SHIFT_BLOCK_1_result), .COUT(RIGHT_SHIFT_BLOCK_1_cout));
  LEFT_SHIFT_BLOCK LEFT_SHIFT_BLOCK_1 (
    .OP_IN(OP0_A_BUS), .SHIFT_DISTANCE(OP1_B_BUS[4:0]), .SHIFT_FUNC_SEL(ALU_CTRL_BUS[4:3]),
    .RESULT(LEFT_SHIFT_BLOCK_1_result));
  Multiplexer #(.select(3), .width(32), .enable("false")) multiplexer_2 (
    .in0(ALU_ADDER_1_result), .in1(and_1_out), .in2(or_1_out), .in3(xor_1_out),
    .in4(RIGHT_SHIFT_BLOCK_1_result), .in5(LEFT_SHIFT_BLOCK_1_result), .in6(OP1_B_BUS), .out(RESULT),
    .sel(ALU_CTRL_BUS[2:0]));  // open: in7
  and and_2 (and_2_out, ALU_CTRL_BUS[0], ~ALU_CTRL_BUS[1], ALU_CTRL_BUS[2], ALU_CTRL_BUS[3], ALU_CTRL_BUS[4]);  // AND_Gate
  Multiplexer #(.enable("false")) multiplexer_3 (
    .in0(ALU_ADDER_1_cout), .in1(RIGHT_SHIFT_BLOCK_1_cout), .out(FLAG[1]), .sel(and_2_out));
  Comparator #(.width(32)) comparator_1 (.a(RESULT), .b({32{1'b0}}), .eq(FLAG[2]), .lt(FLAG[3]));  // open: gt
endmodule

module State_machine (
  input  CLK,
  input  STATE_CLR,
  input  CPU_EN,
  input  COND_MATCHED,
  input  [31:0] INSTRUCTION,
  output [3:0] STATE
);

  wire and_1_out, and_2_out, and_3_out, and_4_out, and_5_out, and_6_out, and_7_out, and_8_out, and_9_out,
       and_10_out, and_11_out, and_12_out, and_13_out, and_14_out, and_15_out, and_16_out, and_17_out,
       not_1_out, not_2_out, not_3_out, not_4_out, not_5_out, not_6_out, not_7_out, not_8_out, not_9_out,
       not_10_out, not_11_out, not_12_out, not_13_out, not_14_out, not_15_out, not_16_out, not_17_out,
       not_18_out, not_19_out, not_20_out, not_21_out, not_22_out, not_23_out, not_24_out, not_25_out,
       not_26_out, not_27_out, not_28_out, not_29_out, not_30_out, not_31_out, not_32_out, not_33_out,
       not_34_out, not_35_out, not_36_out, not_37_out, not_38_out, not_39_out, not_40_out, not_41_out,
       not_42_out, not_43_out, not_44_out, not_45_out, not_46_out, not_47_out, not_48_out, not_49_out,
       not_50_out, not_51_out, not_52_out, not_53_out, not_54_out, not_55_out, not_56_out, not_57_out,
       not_58_out, not_59_out, not_60_out, not_61_out;
  wire [3:0] or_4_out;

  Register #(.width(4)) register_1 (.D(or_4_out), .en(1'b1), .clk(CLK), .Q(STATE), .clr(STATE_CLR));
  not not_1 (not_1_out, STATE[3]);
  not not_2 (not_2_out, STATE[2]);
  not not_3 (not_3_out, STATE[1]);
  not not_4 (not_4_out, INSTRUCTION[26]);
  not not_5 (not_5_out, STATE[3]);
  not not_6 (not_6_out, STATE[2]);
  not not_7 (not_7_out, STATE[1]);
  not not_8 (not_8_out, INSTRUCTION[25]);
  not not_9 (not_9_out, INSTRUCTION[24]);
  not not_10 (not_10_out, STATE[3]);
  not not_11 (not_11_out, STATE[2]);
  not not_12 (not_12_out, STATE[1]);
  not not_13 (not_13_out, INSTRUCTION[25]);
  not not_14 (not_14_out, INSTRUCTION[22]);
  not not_15 (not_15_out, STATE[3]);
  not not_16 (not_16_out, STATE[2]);
  not not_17 (not_17_out, STATE[1]);
  not not_18 (not_18_out, INSTRUCTION[23]);
  not not_19 (not_19_out, STATE[2]);
  not not_20 (not_20_out, STATE[0]);
  not not_21 (not_21_out, STATE[3]);
  not not_22 (not_22_out, STATE[2]);
  not not_23 (not_23_out, STATE[1]);
  not not_24 (not_24_out, INSTRUCTION[24]);
  not not_25 (not_25_out, STATE[3]);
  not not_26 (not_26_out, STATE[2]);
  not not_27 (not_27_out, STATE[1]);
  not not_28 (not_28_out, INSTRUCTION[23]);
  not not_29 (not_29_out, INSTRUCTION[22]);
  not not_30 (not_30_out, STATE[2]);
  not not_31 (not_31_out, STATE[0]);
  not not_32 (not_32_out, STATE[3]);
  not not_33 (not_33_out, STATE[2]);
  not not_34 (not_34_out, STATE[1]);
  not not_35 (not_35_out, INSTRUCTION[24]);
  not not_36 (not_36_out, INSTRUCTION[23]);
  not not_37 (not_37_out, STATE[3]);
  not not_38 (not_38_out, STATE[2]);
  not not_39 (not_39_out, STATE[1]);
  not not_40 (not_40_out, INSTRUCTION[24]);
  not not_41 (not_41_out, STATE[3]);
  not not_42 (not_42_out, STATE[2]);
  not not_43 (not_43_out, STATE[1]);
  not not_44 (not_44_out, INSTRUCTION[23]);
  not not_45 (not_45_out, STATE[3]);
  not not_46 (not_46_out, STATE[0]);
  not not_47 (not_47_out, STATE[3]);
  not not_48 (not_48_out, STATE[2]);
  not not_49 (not_49_out, STATE[1]);
  not not_50 (not_50_out, INSTRUCTION[24]);
  not not_51 (not_51_out, INSTRUCTION[23]);
  and and_1 (and_1_out, COND_MATCHED, not_1_out, not_2_out, not_3_out, STATE[0], not_4_out);
  and and_2 (and_2_out, COND_MATCHED, not_5_out, not_6_out, not_7_out, STATE[0], not_8_out, not_9_out);
  and and_3 (and_3_out, COND_MATCHED, not_10_out, not_11_out, not_12_out, STATE[0], not_13_out, not_14_out);
  and and_4 (and_4_out, COND_MATCHED, not_15_out, not_16_out, not_17_out, STATE[0], INSTRUCTION[24], not_18_out);
  and and_5 (and_5_out, STATE[3], not_19_out, STATE[1], not_20_out);
  not not_52 (not_52_out, STATE[3]);
  not not_53 (not_53_out, STATE[0]);
  and and_6 (and_6_out, STATE[3], not_30_out, STATE[1], not_31_out);
  and and_7 (and_7_out, COND_MATCHED, not_32_out, not_33_out, not_34_out, STATE[0], INSTRUCTION[26], INSTRUCTION[25], not_35_out, not_36_out);
  and and_8 (and_8_out, COND_MATCHED, not_37_out, not_38_out, not_39_out, STATE[0], INSTRUCTION[26], INSTRUCTION[25], not_40_out, INSTRUCTION[22]);
  and and_9 (and_9_out, COND_MATCHED, not_41_out, not_42_out, not_43_out, STATE[0], INSTRUCTION[26], INSTRUCTION[25], not_44_out, INSTRUCTION[22]);
  and and_10 (and_10_out, COND_MATCHED, not_45_out, STATE[1], not_46_out);
  not not_54 (not_54_out, STATE[3]);
  not not_55 (not_55_out, STATE[0]);
  not not_56 (not_56_out, STATE[3]);
  not not_57 (not_57_out, STATE[0]);
  not not_58 (not_58_out, STATE[3]);
  not not_59 (not_59_out, STATE[2]);
  not not_60 (not_60_out, STATE[1]);
  not not_61 (not_61_out, STATE[0]);
  or or_1 (or_4_out[3], and_1_out, and_2_out, and_3_out, and_4_out, and_5_out);
  and and_11 (and_11_out, COND_MATCHED, not_21_out, not_22_out, not_23_out, STATE[0], INSTRUCTION[26], INSTRUCTION[25], not_24_out, INSTRUCTION[23]);
  and and_12 (and_12_out, COND_MATCHED, not_25_out, not_26_out, not_27_out, STATE[0], INSTRUCTION[26], INSTRUCTION[25], INSTRUCTION[24], not_28_out, not_29_out);
  or or_2 (or_4_out[2], and_11_out, and_12_out, and_13_out);
  and and_13 (and_13_out, COND_MATCHED, not_52_out, STATE[2], not_53_out);
  or or_3 (or_4_out[1], and_6_out, and_7_out, and_8_out, and_9_out, and_10_out);
  and and_14 (and_14_out, COND_MATCHED, not_47_out, not_48_out, not_49_out, STATE[0], INSTRUCTION[26], INSTRUCTION[25], not_50_out, not_51_out, INSTRUCTION[22]);
  and and_15 (and_15_out, COND_MATCHED, not_54_out, STATE[1], not_55_out);
  and and_16 (and_16_out, COND_MATCHED, not_56_out, STATE[2], not_57_out);
  and and_17 (and_17_out, CPU_EN, not_58_out, not_59_out, not_60_out, not_61_out);
  or or_4 (or_4_out[0], and_14_out, and_15_out, and_16_out, and_17_out);
endmodule

module PC_RAM_DECODER (
  input  CPU_EN,
  input  [3:0] STATE,
  output ROM_CLKEN,
  output PC_REG_EN,
  output PC_SRC_SEL,
  output [3:0] RAM_INT_CTRL
);

  wire not_1_out, not_2_out, not_3_out, not_4_out, not_5_out, not_6_out, not_7_out, not_8_out, not_9_out,
       not_10_out, not_11_out, not_12_out, not_13_out, not_14_out, not_15_out, not_16_out;

  not not_1 (not_1_out, STATE[3]);
  not not_2 (not_2_out, STATE[2]);
  not not_3 (not_3_out, STATE[1]);
  not not_4 (not_4_out, STATE[0]);
  not not_5 (not_5_out, STATE[3]);
  and and_1 (PC_REG_EN, not_5_out, not_6_out, STATE[0]);
  not not_6 (not_6_out, STATE[2]);
  not not_7 (not_7_out, STATE[3]);
  not not_8 (not_8_out, STATE[2]);
  not not_9 (not_9_out, STATE[3]);
  not not_10 (not_10_out, STATE[1]);
  not not_11 (not_11_out, STATE[3]);
  not not_12 (not_12_out, STATE[1]);
  not not_13 (not_13_out, STATE[0]);
  not not_14 (not_14_out, STATE[3]);
  and and_2 (RAM_INT_CTRL[2], not_14_out, STATE[2], not_15_out);
  not not_15 (not_15_out, STATE[1]);
  not not_16 (not_16_out, STATE[3]);
  and and_3 (RAM_INT_CTRL[3], not_16_out, STATE[2]);
  and and_4 (ROM_CLKEN, CPU_EN, not_1_out, not_2_out, not_3_out, not_4_out);
  and and_5 (PC_SRC_SEL, not_7_out, not_8_out, STATE[1], STATE[0]);
  and and_6 (RAM_INT_CTRL[0], not_9_out, STATE[2], not_10_out, STATE[0]);
  and and_7 (RAM_INT_CTRL[1], not_11_out, STATE[2], not_12_out, not_13_out);
endmodule

module PROCESSOR_CTRL_UNIT (
  input  CLK,
  input  ASYS_CLR,
  input  CPU_EN,
  input  [31:0] INSTRUCTION,
  input  [3:0] RESULT_FLAG,
  output ROM_CLKEN,
  output [3:0] RAM_INT_CTRL,
  output PC_SRC_SEL,
  output PC_REG_EN,
  output [3:0] REG_RD_SEL,
  output [3:0] OP0_REG_OUT_SEL,
  output [3:0] OP1_REG_OUT_SEL,
  output [1:0] B_BUS_SRC_SEL,
  output REG_IN_BUS_SRC_SEL,
  output DOUT,
  output [8:0] ALU_CTRL,
  output [3:0] FLAG_OUT
);

  wire COND_FLAG_CHK_1_condition_matched;
  wire [2:0] CTRL_DECODER_1_flag_reg_ctrl;
  wire [3:0] State_machine_1_state;

  State_machine State_machine_1 (
    .CLK(CLK), .STATE_CLR(ASYS_CLR), .CPU_EN(CPU_EN), .COND_MATCHED(COND_FLAG_CHK_1_condition_matched),
    .INSTRUCTION(INSTRUCTION), .STATE(State_machine_1_state));
  FLAG_REGISTER FLAG_REGISTER_1 (
    .FLAG_EN_CTRL(CTRL_DECODER_1_flag_reg_ctrl), .FLAG_IN(RESULT_FLAG), .CLR_FLAG(ASYS_CLR), .CLK(CLK),
    .FLAG_OUT(FLAG_OUT));
  COND_FLAG_CHK COND_FLAG_CHK_1 (
    .CONDITION_IN(INSTRUCTION[31:28]), .FLAG_IN(FLAG_OUT),
    .CONDITION_MATCHED(COND_FLAG_CHK_1_condition_matched));
  // Probe on State_machine_1_state
  PC_RAM_DECODER PC_RAM_DECODER_1 (
    .CPU_EN(CPU_EN), .STATE(State_machine_1_state), .ROM_CLKEN(ROM_CLKEN), .PC_REG_EN(PC_REG_EN),
    .PC_SRC_SEL(PC_SRC_SEL), .RAM_INT_CTRL(RAM_INT_CTRL));
  CTRL_DECODER CTRL_DECODER_1 (
    .STATE(State_machine_1_state), .INST(INSTRUCTION), .C_FLAG(FLAG_OUT[1]), .ALU_CTRL(ALU_CTRL),
    .FLAG_REG_CTRL(CTRL_DECODER_1_flag_reg_ctrl), .RD_OUT(REG_RD_SEL), .OP0_REG_OUT_SEL(OP0_REG_OUT_SEL),
    .OP1_REG_OUT_SEL(OP1_REG_OUT_SEL), .B_BUS_SRC_SEL(B_BUS_SRC_SEL), .REG_INPUT_SRC_SEL(REG_IN_BUS_SRC_SEL),
    .DOUT(DOUT));
endmodule

module ALU_ADDER (
  input  Cin,
  input  RSB,
  input  SUB,
  input  [31:0] OP0,
  input  [31:0] OP1,
  output [31:0] RESULT,
  output Cout,
  output V
);

  wire adder_1_cout, multiplexer_3_out, not_3_out, or_1_out;
  wire [31:0] multiplexer_1_out, multiplexer_2_out, not_1_out, not_2_out;

  assign not_1_out = ~OP0;  // NOT_Gate not_1, 32 bits wide
  assign not_2_out = ~OP1;  // NOT_Gate not_2, 32 bits wide
  Multiplexer #(.width(32), .enable("false")) multiplexer_1 (
    .in0(OP0), .in1(not_1_out), .out(multiplexer_1_out), .sel(RSB));
  Multiplexer #(.width(32), .enable("false")) multiplexer_2 (
    .in0(OP1), .in1(not_2_out), .out(multiplexer_2_out), .sel(SUB));
  not not_3 (not_3_out, Cin);
  or or_1 (or_1_out, RSB, SUB);
  Multiplexer #(.enable("false")) multiplexer_3 (.in0(Cin), .in1(not_3_out), .out(multiplexer_3_out), .sel(or_1_out));
  Adder #(.width(31)) adder_1 (
    .a(multiplexer_1_out[30:0]), .b(multiplexer_2_out[30:0]), .out(RESULT[30:0]), .cin(multiplexer_3_out),
    .cout(adder_1_cout));
  Adder #(.width(1)) adder_2 (
    .a(multiplexer_1_out[31]), .b(multiplexer_2_out[31]), .out(RESULT[31]), .cin(adder_1_cout), .cout(Cout));
  xor xor_1 (V, adder_1_cout, Cout);
endmodule

module CTRL_DECODER (
  input  [3:0] STATE,
  input  [31:0] INST,
  input  C_FLAG,
  output [8:0] ALU_CTRL,
  output [2:0] FLAG_REG_CTRL,
  output [3:0] RD_OUT,
  output [3:0] OP0_REG_OUT_SEL,
  output [3:0] OP1_REG_OUT_SEL,
  output [1:0] B_BUS_SRC_SEL,
  output REG_INPUT_SRC_SEL,
  output DOUT
);

  wire and_1_out, and_2_out, and_3_out, and_4_out, and_5_out, and_6_out, and_7_out, and_8_out, and_9_out,
       and_10_out, and_11_out, and_12_out, and_13_out, and_14_out, and_15_out, and_16_out, and_17_out,
       and_18_out, and_19_out, and_20_out, and_21_out, and_22_out, and_25_out, and_26_out, and_27_out,
       and_28_out, and_29_out, and_30_out, and_31_out, and_32_out, and_33_out, and_34_out, and_35_out,
       and_36_out, and_37_out, and_38_out, and_39_out, and_40_out, and_42_out, and_43_out, and_44_out,
       and_45_out, and_49_out, and_50_out, nand_1_out, nand_2_out, not_1_out, not_2_out, not_3_out,
       not_4_out, not_5_out, not_6_out, not_7_out, not_8_out, not_9_out, not_10_out, not_11_out, not_12_out,
       not_13_out, not_14_out, not_15_out, not_16_out, not_17_out, not_18_out, not_19_out, not_20_out,
       not_21_out, not_22_out, not_23_out, not_24_out, not_25_out, not_26_out, not_27_out, not_28_out,
       not_29_out, not_30_out, not_31_out, not_32_out, not_33_out, not_34_out, not_35_out, not_36_out,
       not_37_out, not_38_out, not_39_out, not_40_out, not_41_out, not_42_out, not_43_out, not_44_out,
       not_45_out, not_46_out, not_47_out, not_48_out, not_49_out, not_50_out, not_51_out, not_52_out,
       not_53_out, not_54_out, not_55_out, not_56_out, not_57_out, not_58_out, not_59_out, not_60_out,
       not_61_out, not_62_out, not_63_out, not_64_out, not_65_out, not_66_out, not_67_out, not_68_out,
       not_69_out, not_70_out, not_71_out, not_72_out, not_73_out, not_74_out, not_75_out, not_76_out,
       not_77_out, not_78_out, not_79_out, not_80_out, not_81_out, not_82_out, not_83_out, not_84_out,
       not_85_out, not_86_out, not_87_out, not_88_out, not_89_out, not_90_out, not_91_out, not_92_out,
       not_93_out, not_94_out, not_95_out, not_96_out, not_97_out, not_98_out, not_99_out, not_100_out,
       not_101_out, not_102_out, not_103_out, not_104_out, not_105_out, not_106_out, not_107_out,
       not_108_out, not_109_out, not_110_out, not_111_out, not_112_out, not_113_out, not_114_out,
       not_115_out, not_116_out, not_117_out, not_118_out, not_119_out, not_120_out, not_121_out,
       not_122_out, not_123_out, not_124_out, not_125_out, not_126_out, not_127_out, not_128_out,
       not_129_out, not_130_out, not_131_out, not_132_out, not_133_out, not_134_out, not_135_out,
       not_136_out, not_137_out, not_138_out, not_139_out, not_140_out, not_141_out, not_142_out,
       not_143_out, not_144_out, not_145_out, not_146_out, not_147_out, not_148_out, not_149_out,
       not_150_out, not_151_out, not_152_out, not_153_out, not_154_out, not_155_out, not_156_out,
       not_157_out, not_158_out, not_159_out, not_160_out, not_161_out, not_162_out, not_163_out,
       not_164_out, not_165_out, not_166_out, not_167_out, not_168_out, not_169_out, not_170_out,
       not_171_out, not_172_out, not_173_out, not_174_out, not_175_out, not_176_out, not_177_out,
       not_178_out, not_179_out, not_180_out, not_181_out, not_182_out, not_183_out, not_184_out,
       not_185_out, not_186_out, not_187_out, not_188_out, not_189_out, or_1_out;
  wire [1:0] and_41_out, or_13_out;

  not not_1 (not_1_out, INST[23]);
  not not_2 (not_2_out, INST[26]);
  not not_3 (not_3_out, INST[24]);
  not not_4 (not_4_out, INST[23]);
  not not_5 (not_5_out, INST[23]);
  not not_6 (not_6_out, STATE[3]);
  not not_7 (not_7_out, STATE[2]);
  not not_8 (not_8_out, STATE[1]);
  not not_9 (not_9_out, STATE[2]);
  not not_10 (not_10_out, STATE[1]);
  not not_11 (not_11_out, INST[26]);
  not not_12 (not_12_out, INST[24]);
  not not_13 (not_13_out, INST[23]);
  not not_14 (not_14_out, STATE[2]);
  not not_15 (not_15_out, STATE[1]);
  not not_16 (not_16_out, STATE[2]);
  not not_17 (not_17_out, STATE[1]);
  not not_18 (not_18_out, INST[24]);
  not not_19 (not_19_out, INST[22]);
  not not_20 (not_20_out, STATE[2]);
  not not_21 (not_21_out, STATE[1]);
  not not_22 (not_22_out, INST[23]);
  not not_23 (not_23_out, INST[22]);
  not not_24 (not_24_out, STATE[2]);
  not not_25 (not_25_out, STATE[1]);
  not not_26 (not_26_out, STATE[2]);
  not not_27 (not_27_out, STATE[1]);
  not not_28 (not_28_out, STATE[2]);
  not not_29 (not_29_out, STATE[1]);
  not not_30 (not_30_out, STATE[0]);
  not not_31 (not_31_out, INST[25]);
  not not_32 (not_32_out, INST[24]);
  not not_33 (not_33_out, STATE[2]);
  not not_34 (not_34_out, STATE[1]);
  not not_35 (not_35_out, STATE[0]);
  not not_36 (not_36_out, INST[25]);
  not not_37 (not_37_out, INST[22]);
  not not_38 (not_38_out, STATE[2]);
  not not_39 (not_39_out, STATE[1]);
  not not_40 (not_40_out, STATE[0]);
  not not_41 (not_41_out, INST[25]);
  not not_42 (not_42_out, INST[23]);
  not not_43 (not_43_out, STATE[2]);
  not not_44 (not_44_out, STATE[1]);
  not not_45 (not_45_out, STATE[0]);
  not not_46 (not_46_out, INST[25]);
  not not_47 (not_47_out, INST[22]);
  not not_48 (not_48_out, STATE[2]);
  not not_49 (not_49_out, STATE[1]);
  not not_50 (not_50_out, STATE[0]);
  not not_51 (not_51_out, INST[25]);
  not not_52 (not_52_out, INST[22]);
  not not_53 (not_53_out, STATE[2]);
  not not_54 (not_54_out, STATE[1]);
  not not_55 (not_55_out, STATE[0]);
  not not_56 (not_56_out, INST[26]);
  not not_57 (not_57_out, INST[25]);
  not not_58 (not_58_out, INST[23]);
  not not_59 (not_59_out, C_FLAG);
  not not_60 (not_60_out, STATE[2]);
  not not_61 (not_61_out, STATE[1]);
  not not_62 (not_62_out, STATE[0]);
  not not_63 (not_63_out, INST[26]);
  not not_64 (not_64_out, INST[25]);
  not not_65 (not_65_out, STATE[2]);
  not not_66 (not_66_out, STATE[1]);
  not not_67 (not_67_out, STATE[0]);
  not not_68 (not_68_out, INST[26]);
  not not_69 (not_69_out, INST[25]);
  not not_70 (not_70_out, INST[25]);
  not not_71 (not_71_out, INST[24]);
  not not_72 (not_72_out, STATE[2]);
  not not_73 (not_73_out, STATE[1]);
  not not_74 (not_74_out, STATE[0]);
  not not_75 (not_75_out, INST[26]);
  not not_76 (not_76_out, INST[22]);
  not not_77 (not_77_out, STATE[2]);
  not not_78 (not_78_out, STATE[1]);
  not not_79 (not_79_out, STATE[0]);
  not not_80 (not_80_out, INST[26]);
  not not_81 (not_81_out, INST[24]);
  not not_82 (not_82_out, STATE[2]);
  not not_83 (not_83_out, STATE[1]);
  not not_84 (not_84_out, STATE[0]);
  not not_85 (not_85_out, INST[26]);
  not not_86 (not_86_out, STATE[2]);
  not not_87 (not_87_out, STATE[1]);
  not not_88 (not_88_out, STATE[0]);
  not not_89 (not_89_out, INST[26]);
  not not_90 (not_90_out, INST[24]);
  not not_91 (not_91_out, STATE[2]);
  not not_92 (not_92_out, STATE[1]);
  not not_93 (not_93_out, STATE[0]);
  not not_94 (not_94_out, INST[26]);
  not not_95 (not_95_out, INST[25]);
  not not_96 (not_96_out, STATE[2]);
  not not_97 (not_97_out, STATE[1]);
  not not_98 (not_98_out, STATE[0]);
  not not_99 (not_99_out, INST[26]);
  not not_100 (not_100_out, INST[25]);
  not not_101 (not_101_out, INST[24]);
  not not_102 (not_102_out, STATE[2]);
  not not_103 (not_103_out, STATE[1]);
  not not_104 (not_104_out, STATE[0]);
  not not_105 (not_105_out, INST[25]);
  not not_106 (not_106_out, INST[22]);
  not not_107 (not_107_out, STATE[2]);
  not not_108 (not_108_out, STATE[1]);
  not not_109 (not_109_out, STATE[0]);
  not not_110 (not_110_out, INST[26]);
  not not_111 (not_111_out, INST[24]);
  not not_112 (not_112_out, STATE[2]);
  not not_113 (not_113_out, STATE[1]);
  not not_114 (not_114_out, STATE[0]);
  not not_115 (not_115_out, INST[26]);
  not not_116 (not_116_out, INST[25]);
  not not_117 (not_117_out, STATE[2]);
  not not_118 (not_118_out, STATE[1]);
  not not_119 (not_119_out, STATE[0]);
  not not_120 (not_120_out, INST[26]);
  not not_121 (not_121_out, INST[25]);
  not not_122 (not_122_out, INST[24]);
  not not_123 (not_123_out, STATE[3]);
  not not_124 (not_124_out, STATE[2]);
  not not_125 (not_125_out, STATE[0]);
  not not_126 (not_126_out, STATE[3]);
  not not_127 (not_127_out, STATE[2]);
  not not_128 (not_128_out, STATE[1]);
  not not_129 (not_129_out, STATE[0]);
  not not_130 (not_130_out, INST[26]);
  not not_131 (not_131_out, INST[25]);
  not not_132 (not_132_out, STATE[2]);
  not not_133 (not_133_out, STATE[1]);
  not not_134 (not_134_out, STATE[0]);
  not not_135 (not_135_out, INST[26]);
  not not_136 (not_136_out, STATE[2]);
  not not_137 (not_137_out, STATE[1]);
  not not_138 (not_138_out, STATE[0]);
  not not_139 (not_139_out, INST[25]);
  not not_140 (not_140_out, INST[24]);
  not not_141 (not_141_out, STATE[2]);
  not not_142 (not_142_out, STATE[1]);
  not not_143 (not_143_out, STATE[0]);
  not not_144 (not_144_out, INST[25]);
  not not_145 (not_145_out, INST[23]);
  not not_146 (not_146_out, STATE[2]);
  not not_147 (not_147_out, STATE[1]);
  not not_148 (not_148_out, STATE[0]);
  not not_149 (not_149_out, INST[25]);
  not not_150 (not_150_out, INST[22]);
  not not_151 (not_151_out, STATE[3]);
  not not_152 (not_152_out, STATE[2]);
  not not_153 (not_153_out, STATE[0]);
  not not_154 (not_154_out, STATE[3]);
  not not_155 (not_155_out, STATE[2]);
  not not_156 (not_156_out, INST[24]);
  not not_157 (not_157_out, INST[23]);
  not not_158 (not_158_out, STATE[3]);
  not not_159 (not_159_out, STATE[2]);
  not not_160 (not_160_out, STATE[0]);
  not not_161 (not_161_out, STATE[3]);
  not not_162 (not_162_out, STATE[1]);
  not not_163 (not_163_out, STATE[0]);
  not not_164 (not_164_out, STATE[3]);
  not not_165 (not_165_out, STATE[2]);
  not not_166 (not_166_out, STATE[0]);
  not not_167 (not_167_out, STATE[2]);
  not not_168 (not_168_out, STATE[1]);
  not not_169 (not_169_out, STATE[0]);
  not not_170 (not_170_out, INST[26]);
  not not_171 (not_171_out, INST[26]);
  not not_172 (not_172_out, STATE[3]);
  not not_173 (not_173_out, STATE[1]);
  not not_174 (not_174_out, STATE[0]);
  not not_175 (not_175_out, STATE[3]);
  and and_1 (and_1_out, INST[25], INST[24], not_1_out, INST[22]);
  not not_176 (not_176_out, STATE[3]);
  and and_2 (and_2_out, not_2_out, not_3_out, not_4_out, INST[22]);
  and and_3 (and_3_out, INST[25], INST[24], not_5_out);
  and and_4 (and_4_out, INST[25], INST[24], INST[22]);
  and and_5 (and_5_out, INST[26], INST[24], INST[23], INST[22]);
  and and_6 (and_6_out, INST[26], INST[25]);
  and and_7 (and_7_out, not_6_out, not_7_out, not_8_out);
  and and_8 (and_8_out, not_9_out, not_10_out, not_11_out, not_12_out, not_13_out);
  and and_9 (and_9_out, not_14_out, not_15_out, INST[25], INST[24], INST[23]);
  and and_10 (and_10_out, not_16_out, not_17_out, INST[26], not_18_out, not_19_out);
  and and_11 (and_11_out, not_20_out, not_21_out, INST[26], not_22_out, not_23_out);
  and and_12 (and_12_out, not_24_out, not_25_out, INST[26], INST[24], INST[23], INST[22]);
  and and_13 (and_13_out, not_26_out, not_27_out, INST[26], INST[25]);
  and and_14 (and_14_out, STATE[3], STATE[0]);
  and and_15 (and_15_out, STATE[3], STATE[1]);
  and and_16 (and_16_out, STATE[3], not_28_out, not_29_out, not_30_out, INST[26], not_31_out, not_32_out, INST[23]);
  and and_17 (and_17_out, STATE[3], not_33_out, not_34_out, not_35_out, INST[26], not_36_out, INST[23], not_37_out);
  and and_18 (and_18_out, STATE[3], not_38_out, not_39_out, not_40_out, INST[26], not_41_out, INST[24], not_42_out);
  and and_19 (and_19_out, STATE[3], not_43_out, not_44_out, not_45_out, INST[26], not_46_out, INST[24], not_47_out);
  and and_20 (and_20_out, C_FLAG, STATE[3], not_48_out, not_49_out, not_50_out, INST[26], not_51_out, INST[24], INST[23], not_52_out);
  and and_21 (and_21_out, C_FLAG, STATE[3], not_53_out, not_54_out, not_55_out, not_56_out, not_57_out, INST[24], not_58_out, INST[22]);
  and and_22 (and_22_out, not_59_out, STATE[3], not_60_out, not_61_out, not_62_out, not_63_out, not_64_out, INST[24], INST[23]);
  and and_23 (ALU_CTRL[6], STATE[3], not_65_out, not_66_out, not_67_out, not_68_out, not_69_out, INST[23], INST[22]);
  not not_177 (not_177_out, INST[22]);
  or or_1 (or_1_out, not_70_out, not_71_out);
  not not_178 (not_178_out, INST[26]);
  not not_179 (not_179_out, STATE[0]);
  not not_180 (not_180_out, STATE[1]);
  not not_181 (not_181_out, STATE[2]);
  and and_24 (ALU_CTRL[8], STATE[3], not_72_out, not_73_out, not_74_out, not_75_out, INST[25], INST[24], INST[23], not_76_out);
  and and_25 (and_25_out, STATE[3], not_77_out, not_78_out, not_79_out, not_80_out, INST[25], not_81_out);
  and and_26 (and_26_out, INST[21], STATE[3], not_82_out, not_83_out, not_84_out, not_85_out);
  and and_27 (and_27_out, STATE[3], not_86_out, not_87_out, not_88_out, not_89_out, INST[25], not_90_out, INST[23]);
  and and_28 (and_28_out, INST[21], STATE[3], not_91_out, not_92_out, not_93_out, not_94_out, not_95_out, INST[24]);
  and and_29 (and_29_out, INST[21], STATE[3], not_96_out, not_97_out, not_98_out, not_99_out, not_100_out, not_101_out, INST[23]);
  and and_30 (and_30_out, STATE[3], not_102_out, not_103_out, not_104_out, INST[26], not_105_out, INST[24], INST[23], not_106_out);
  and and_31 (and_31_out, STATE[3], not_107_out, not_108_out, not_109_out, not_110_out, INST[25], not_111_out, INST[23]);
  and and_32 (and_32_out, INST[21], STATE[3], not_112_out, not_113_out, not_114_out, not_115_out, not_116_out, INST[24]);
  and and_33 (and_33_out, INST[21], STATE[3], not_117_out, not_118_out, not_119_out, not_120_out, not_121_out, not_122_out, INST[23]);
  and and_34 (and_34_out, not_123_out, not_124_out, STATE[1], not_125_out);
  and and_35 (and_35_out, not_126_out, STATE[2], STATE[1], STATE[0]);
  and and_36 (and_36_out, STATE[3], not_127_out, not_128_out, not_129_out, not_130_out, not_131_out);
  and and_37 (and_37_out, STATE[3], not_132_out, not_133_out, not_134_out, not_135_out, INST[25], INST[24]);
  and and_38 (and_38_out, STATE[3], not_136_out, not_137_out, not_138_out, INST[26], not_139_out, not_140_out);
  and and_39 (and_39_out, STATE[3], not_141_out, not_142_out, not_143_out, INST[26], not_144_out, INST[24], not_145_out);
  and and_40 (and_40_out, STATE[3], not_146_out, not_147_out, not_148_out, INST[26], not_149_out, INST[24], INST[23], not_150_out);
  and and_41 (and_41_out[0], not_151_out, not_152_out, STATE[1], not_153_out);
  and and_42 (and_42_out, not_154_out, not_155_out, STATE[1], STATE[0], INST[26], INST[25], not_156_out, not_157_out, INST[22]);
  and and_43 (and_43_out, not_158_out, not_159_out, STATE[1], not_160_out);
  and and_44 (and_44_out, not_161_out, STATE[2], not_162_out, not_163_out);
  and and_45 (and_45_out, not_164_out, not_165_out, STATE[1], not_166_out);
  and and_46 (B_BUS_SRC_SEL[1], STATE[3], not_167_out, not_168_out, not_169_out, not_170_out, INST[25], INST[24], INST[23], INST[22]);
  not not_182 (not_182_out, STATE[2]);
  not not_183 (not_183_out, STATE[1]);
  not not_184 (not_184_out, STATE[0]);
  not not_185 (not_185_out, INST[26]);
  nand nand_1 (nand_1_out, not_171_out, INST[25], INST[24], INST[23], INST[22]);
  not not_186 (not_186_out, STATE[2]);
  not not_187 (not_187_out, STATE[1]);
  not not_188 (not_188_out, STATE[0]);
  not not_189 (not_189_out, INST[25]);
  nand nand_2 (nand_2_out, INST[24], INST[23], INST[22]);
  and and_47 (REG_INPUT_SRC_SEL, not_172_out, STATE[2], STATE[1], STATE[0]);
  or or_2 (ALU_CTRL[2], not_175_out, and_1_out, INST[26], STATE[0], STATE[1], STATE[2]);
  or or_3 (ALU_CTRL[1], not_176_out, and_2_out, and_3_out, and_4_out, and_5_out, and_6_out, STATE[0], STATE[1], STATE[2]);
  or or_4 (ALU_CTRL[0], and_7_out, and_8_out, and_9_out, and_10_out, and_11_out, and_12_out, and_13_out, and_14_out, and_15_out);
  or or_5 (ALU_CTRL[4], and_16_out, and_17_out);
  or or_6 (ALU_CTRL[3], and_18_out, and_19_out);
  or or_7 (ALU_CTRL[5], and_20_out, and_21_out, and_22_out);
  and and_48 (ALU_CTRL[7], STATE[3], INST[23], not_177_out, or_1_out, not_178_out, not_179_out, not_180_out, not_181_out);
  or or_8 (FLAG_REG_CTRL[0], and_25_out, and_26_out);
  or or_9 (FLAG_REG_CTRL[1], and_27_out, and_28_out, and_29_out, and_30_out);
  or or_10 (FLAG_REG_CTRL[2], and_31_out, and_32_out, and_33_out);
  or or_11 (and_41_out[1], and_34_out, and_35_out, and_36_out, and_37_out, and_38_out, and_39_out, and_40_out);
  or or_12 (or_13_out[1], and_42_out, and_43_out);
  or or_13 (or_13_out[0], and_44_out, and_45_out);
  and and_49 (and_49_out, INST[27], STATE[3], not_182_out, not_183_out, not_184_out, not_185_out, nand_1_out);
  and and_50 (and_50_out, INST[27], STATE[3], not_186_out, not_187_out, not_188_out, INST[26], not_189_out, nand_2_out);
  and and_51 (DOUT, STATE[3], STATE[2], not_173_out, not_174_out);
  or or_14 (B_BUS_SRC_SEL[0], and_49_out, and_50_out);
  Multiplexer #(.select(2), .width(4), .enable("false")) multiplexer_1 (
    .in0(4'b1111), .in1(4'b1111), .in2(INST[16:13]), .in3(4'b1110), .out(RD_OUT), .sel(and_41_out));
  Multiplexer #(.select(2), .width(4), .enable("false")) multiplexer_2 (
    .in0(INST[12:9]), .in1(INST[20:17]), .in2(4'b1110), .in3(4'b1111), .out(OP1_REG_OUT_SEL), .sel(or_13_out));

  assign OP0_REG_OUT_SEL = INST[20:17];
endmodule
